# Fritzing sketch BME-280 (saved by Fritzing 1.0.5)
breadboards: 1

parts:
  M1 = NEO-6M GPS Module [part_number=GY-GPS6MV2]
  A1 = XIAO ESP32C3-smd
  A2 = GY-BMP280 Breakout

nets:
  N1: M1.GND, A1.Pin_2, A1.Pin_21, A2.Pin_2
  N2: M1.Tx, A1.Pin_16
  N3: M1.Vcc, A1.Pin_22
  N4: A1.Pin_13, A2.Pin_4
  N5: A1.Pin_14, A2.Pin_3
  N6: A1.Pin_20, A2.Pin_1

notes:
  BME-280
  Sensor id: 3
  Datastream id:
  Temperatuur
  Obs. Prop. id: 1
  Thing id:
  Thing name:
  Pressure
  Obs. Prop. id: 4
  Aprox Alt.
  Obs. Prop. id: 3
  Rel. Humidity
  Obs. Prop. id: 2
  UoM:
  hPa
  UoM:
  deg Celsius
  UoM
  m
  UoM:
  % rH

custom parts:
  NEO-6M GPS Module: GY-GPS6MV2 NEO-6M GPS Module Module based on U-blox NEO-6M GPS engine, incorporating regulator for 3.3-5V DC input, MS621FE-compatible rechargeable battery for backup and EEPROM for storing configuration settings. Links: NEO-6 series product information page NEO-6 Datasheet
  XIAO ESP32C3-smd: Seeed Studio XIAO ESP32C3 adopts new RISC-V architecture, supporting both Wi-Fi and BLE wireless connectivities.
