# Fritzing sketch HMC-5883L (saved by Fritzing 1.0.5)
breadboards: 1

parts:
  M1 = NEO-6M GPS Module [part_number=GY-GPS6MV2]
  A1 = XIAO ESP32C3-smd
  Module1 = Boladge HMC5883L Compass Module  # not connected

nets:
  N1: M1.GND, A1.Pin_21
  N2: M1.Tx, A1.Pin_16
  N3: M1.Vcc, A1.Pin_22

notes:
  Heading/Angle
  Obs. Prop. id: 10
  Datastream id:
  HMC-5883L
  Sensor id: 4
  Thing id:
  Thing name:
  UoM:
  degrees

custom parts:
  NEO-6M GPS Module: GY-GPS6MV2 NEO-6M GPS Module Module based on U-blox NEO-6M GPS engine, incorporating regulator for 3.3-5V DC input, MS621FE-compatible rechargeable battery for backup and EEPROM for storing configuration settings. Links: NEO-6 series product information page NEO-6 Datasheet
  XIAO ESP32C3-smd: Seeed Studio XIAO ESP32C3 adopts new RISC-V architecture, supporting both Wi-Fi and BLE wireless connectivities.
  Boladge HMC5883L Compass Module: Cheap digital compass module
