# Fritzing sketch MB-090 (saved by Fritzing 1.0.5)
breadboards: 1

parts:
  M1 = NEO-6M GPS Module [part_number=GY-GPS6MV2]
  A1 = XIAO ESP32C3-smd
  R2 = Basic Flex Resistor
  R3 = Resistor [tolerance=±5% resistance=10k package="1206 [SMD]"]

nets:
  N1: M1.GND, A1.Pin_21, R3.Pin_1
  N2: M1.Tx, A1.Pin_16
  N3: M1.Vcc, A1.Pin_22
  N4: A1.Pin_9, R2.Pin_2, R3.Pin_0
  N5: A1.Pin_20, R2.pin_1

notes:
  Bend Resistance
  Obs. Prop. id: 16
  Datastream id:
  MB-090
  Sensor id: 10
  Thing id:
  Thing name:
  UoM:
  ohm

custom parts:
  NEO-6M GPS Module: GY-GPS6MV2 NEO-6M GPS Module Module based on U-blox NEO-6M GPS engine, incorporating regulator for 3.3-5V DC input, MS621FE-compatible rechargeable battery for backup and EEPROM for storing configuration settings. Links: NEO-6 series product information page NEO-6 Datasheet
  XIAO ESP32C3-smd: Seeed Studio XIAO ESP32C3 adopts new RISC-V architecture, supporting both Wi-Fi and BLE wireless connectivities.
