# Fritzing sketch RCWL-1604 (saved by Fritzing 1.0.5)
breadboards: 1

parts:
  M1 = NEO-6M GPS Module [part_number=GY-GPS6MV2]
  A1 = XIAO ESP32C3-smd
  HC-SR04_Sensor_2 = HC-SR04 Ultrasonic Distance Sensor

nets:
  GND: M1.GND, A1.Pin_2, A1.Pin_21, HC-SR04_Sensor_2.GND
  N1: M1.Tx, A1.Pin_16
  N2: M1.Vcc, A1.Pin_22
  N3: A1.Pin_11, HC-SR04_Sensor_2.TRIG
  N4: A1.Pin_12, HC-SR04_Sensor_2.ECHO
  N5: A1.Pin_20, HC-SR04_Sensor_2.VCC

notes:
  Distance
  Obs. Prop. id: 7
  Datastream id:
  RCWL-1604
  Sensor id: 8
  Thing id:
  Thing name:
  UoM:
  cm

custom parts:
  NEO-6M GPS Module: GY-GPS6MV2 NEO-6M GPS Module Module based on U-blox NEO-6M GPS engine, incorporating regulator for 3.3-5V DC input, MS621FE-compatible rechargeable battery for backup and EEPROM for storing configuration settings. Links: NEO-6 series product information page NEO-6 Datasheet
  XIAO ESP32C3-smd: Seeed Studio XIAO ESP32C3 adopts new RISC-V architecture, supporting both Wi-Fi and BLE wireless connectivities.
