# Fritzing sketch ADXL-345 (saved by Fritzing 1.0.5)
breadboards: 1

parts:
  M1 = NEO-6M GPS Module [part_number=GY-GPS6MV2]
  A1 = XIAO ESP32C3-smd
  Part2 = Triple Axis Accelerometer Breakout - ADXL345

nets:
  GND: M1.GND, A1.Pin_2, A1.Pin_21, Part2.GND
  N1: M1.Tx, A1.Pin_16
  N2: M1.Vcc, A1.Pin_22
  N3: A1.Pin_13, Part2.SDA
  N4: A1.Pin_14, Part2.SCL
  N5: A1.Pin_20, Part2.VCC

notes:
  ADXL-345
  Sensor id: 1
  Thing name:
  Accelerometer
  Obs Prop id: 9
  Thing id:
  Datastream id:
  UoM:
  m/s^2

custom parts:
  NEO-6M GPS Module: GY-GPS6MV2 NEO-6M GPS Module Module based on U-blox NEO-6M GPS engine, incorporating regulator for 3.3-5V DC input, MS621FE-compatible rechargeable battery for backup and EEPROM for storing configuration settings. Links: NEO-6 series product information page NEO-6 Datasheet
  XIAO ESP32C3-smd: Seeed Studio XIAO ESP32C3 adopts new RISC-V architecture, supporting both Wi-Fi and BLE wireless connectivities.
