# Fritzing sketch AHT-21B (saved by Fritzing 1.0.5)
breadboards: 1

parts:
  M1 = NEO-6M GPS Module [part_number=GY-GPS6MV2]
  A1 = XIAO ESP32C3-smd
  AHT1 = AHT20 BMP280 pressure and humidity breakout

nets:
  GND: M1.GND, A1.Pin_2, A1.Pin_21, AHT1.GND
  N1: M1.Tx, A1.Pin_16
  N2: M1.Vcc, A1.Pin_22
  N3: A1.Pin_13, AHT1.SDA
  N4: A1.Pin_14, AHT1.SCL
  N5: A1.Pin_20, AHT1.VDD

notes:
  Temperature
  Obs Prop id: 1
  Datastream id:
  AHT-21B
  Sensor id: 2
  Thing id:
  Thing name:
  Rel. Humudity
  Obs Prop id: 2
  UoM:
  deg Celsius
  UoM
  % rH

custom parts:
  NEO-6M GPS Module: GY-GPS6MV2 NEO-6M GPS Module Module based on U-blox NEO-6M GPS engine, incorporating regulator for 3.3-5V DC input, MS621FE-compatible rechargeable battery for backup and EEPROM for storing configuration settings. Links: NEO-6 series product information page NEO-6 Datasheet
  XIAO ESP32C3-smd: Seeed Studio XIAO ESP32C3 adopts new RISC-V architecture, supporting both Wi-Fi and BLE wireless connectivities.
  AHT20 BMP280 pressure and humidity breakout: Cheap breakout board for the BMP280, barometric pressure sensor, and AHT20, humidity sensor
