# Fritzing sketch HW-390 (saved by Fritzing 1.0.5)
breadboards: 1

parts:
  M1 = NEO-6M GPS Module [part_number=GY-GPS6MV2]
  A1 = XIAO ESP32C3-smd
  Capacitive_Soil_Moisture_Sensor2 = DFRobot Capacitive Soil Moisture Sensor V1.0 [part_number=SEN0193]

nets:
  GND: M1.GND, A1.Pin_2, A1.Pin_21, Capacitive_Soil_Moisture_Sensor2.GND
  N1: M1.Tx, A1.Pin_16
  N2: M1.Vcc, A1.Pin_22
  N3: A1.Pin_9, Capacitive_Soil_Moisture_Sensor2.A
  N4: A1.Pin_20, Capacitive_Soil_Moisture_Sensor2.VCC

notes:
  Rel Humidity
  Obs. Prop. id: 2
  Datastream id:
  HW-390
  Sensor id: 11
  Thing id:
  Thing name:
  UoM:
  % rH

custom parts:
  NEO-6M GPS Module: GY-GPS6MV2 NEO-6M GPS Module Module based on U-blox NEO-6M GPS engine, incorporating regulator for 3.3-5V DC input, MS621FE-compatible rechargeable battery for backup and EEPROM for storing configuration settings. Links: NEO-6 series product information page NEO-6 Datasheet
  XIAO ESP32C3-smd: Seeed Studio XIAO ESP32C3 adopts new RISC-V architecture, supporting both Wi-Fi and BLE wireless connectivities.
  DFRobot Capacitive Soil Moisture Sensor V1.0: DFRobot Capacitive Soil Moisture Sensor V1.0 This product measures soil moisture levels by capacitive sensing, rather than resistive sensing like other types of moisture sensor. It is made of a corrosion resistant material giving it a long service life. Insert it into soil and impress your friends with the real-time soil moisture data! The product includes an on-board voltage regulator which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
