# Fritzing sketch MAX-30102 (saved by Fritzing 1.0.5)
breadboards: 1

parts:
  M1 = NEO-6M GPS Module [part_number=GY-GPS6MV2]
  A1 = XIAO ESP32C3-smd
  M2 = MakerFocus MAX30102

nets:
  GND: M1.GND, A1.Pin_2, A1.Pin_21, M2.GND
  N1: M1.Tx, A1.Pin_16
  N2: M1.Vcc, A1.Pin_22
  N3: A1.Pin_13, M2.SDA
  N4: A1.Pin_14, M2.SCL
  N5: A1.Pin_20, M2.VIN

notes:
  Heart Rate
  Obs. Prop. id: 14
  Datastream id:
  MAX-30102
  Sensor id: 6
  Thing id:
  Thing name:
  SpO2
  Obs. Prop. id: 5
  UoM:
  bpm
  UoM:
  SpO2

custom parts:
  NEO-6M GPS Module: GY-GPS6MV2 NEO-6M GPS Module Module based on U-blox NEO-6M GPS engine, incorporating regulator for 3.3-5V DC input, MS621FE-compatible rechargeable battery for backup and EEPROM for storing configuration settings. Links: NEO-6 series product information page NEO-6 Datasheet
  XIAO ESP32C3-smd: Seeed Studio XIAO ESP32C3 adopts new RISC-V architecture, supporting both Wi-Fi and BLE wireless connectivities.
  MakerFocus MAX30102: Oximeter module using the MAX30102 chip. As usual, if you want the mounting holes in pcb, you need to drag a hole over the pad in silkscreen to actually drill the hole (by default they are not drilled)
