# Fritzing sketch SEN-0564 (saved by Fritzing 1.0.5)
breadboards: 1

parts:
  M1 = NEO-6M GPS Module [part_number=GY-GPS6MV2]
  A1 = XIAO ESP32C3-smd
  A2 = dfr-SEN0564

nets:
  N1: M1.GND, A1.Pin_2, A1.Pin_21, A2.Pin_3
  N2: M1.Tx, A1.Pin_16
  N3: M1.Vcc, A1.Pin_22
  N4: A1.Pin_9, A2.Pin_1
  N5: A1.Pin_20, A2.Pin_2

notes:
  CO/Gas
  Obs. Prop. id: 17
  Datastream id:
  SEN-0564
  Sensor id: 13
  Thing id:
  Thing name:
  UoM:
  %

custom parts:
  NEO-6M GPS Module: GY-GPS6MV2 NEO-6M GPS Module Module based on U-blox NEO-6M GPS engine, incorporating regulator for 3.3-5V DC input, MS621FE-compatible rechargeable battery for backup and EEPROM for storing configuration settings. Links: NEO-6 series product information page NEO-6 Datasheet
  XIAO ESP32C3-smd: Seeed Studio XIAO ESP32C3 adopts new RISC-V architecture, supporting both Wi-Fi and BLE wireless connectivities.
  dfr-SEN0564: Fermion: MEMS CO sensor employs state-of-the-art microelectromechanical system (MEMS) technology, endowing the sensor with compact dimensions (13x13x2.5mm), low power consumption (<20mA), minimal heat generation, short preheating time, and swift response recovery.
