# Fritzing sketch TTP-223B (saved by Fritzing 1.0.5)
breadboards: 1

parts:
  M1 = NEO-6M GPS Module [part_number=GY-GPS6MV2]
  A1 = XIAO ESP32C3-smd
  Sensor1 = TTP223B Capacitive Touch Sensor Module

nets:
  GND: M1.GND, A1.Pin_2, A1.Pin_21, Sensor1.GND
  N1: M1.Tx, A1.Pin_16
  N2: M1.Vcc, A1.Pin_22
  N3: A1.Pin_11, Sensor1.SIG
  N4: A1.Pin_20, Sensor1.VCC

notes:
  State
  Obs. Prop. id: 18
  Datastream id:
  TTP-223B
  Sensor id: 14
  Thing id:
  Thing name:
  UoM:
  bool

custom parts:
  NEO-6M GPS Module: GY-GPS6MV2 NEO-6M GPS Module Module based on U-blox NEO-6M GPS engine, incorporating regulator for 3.3-5V DC input, MS621FE-compatible rechargeable battery for backup and EEPROM for storing configuration settings. Links: NEO-6 series product information page NEO-6 Datasheet
  XIAO ESP32C3-smd: Seeed Studio XIAO ESP32C3 adopts new RISC-V architecture, supporting both Wi-Fi and BLE wireless connectivities.
  TTP223B Capacitive Touch Sensor Module: The TTP223B capacitive touch sensor module uses the TTP223B IC. The appropriate voltage is approximately 2 to 5.5 volts.
