# Fritzing sketch ESP32C3-sensor (saved by Fritzing 1.0.6)
breadboards: 1

parts:
  A1 = XIAO ESP32C3-smd
  R1 = Resistor [tolerance=±5% power=0.25W resistance=10k package=THT]
  R2 = Resistor [tolerance=±5% power=0.25W resistance=10k package=THT]

nets:
  N1: A1.Pin_13, R1.Pin_0
  N2: A1.Pin_14, R2.Pin_0
  N3: A1.Pin_20, R2.Pin_1

custom parts:
  XIAO ESP32C3-smd: Seeed Studio XIAO ESP32C3 adopts new RISC-V architecture, supporting both Wi-Fi and BLE wireless connectivities.
