# Fritzing sketch ESP32C3-GPSv2 (saved by Fritzing 1.0.6)
breadboards: 1

parts:
  M1 = NEO-6M GPS Module [part_number=GY-GPS6MV2]
  A2 = XIAO ESP32C3-smd
  R3 = Resistor [tolerance=±5% power=0.25W resistance=10k package=THT]
  R4 = Resistor [tolerance=±5% power=0.25W resistance=10k package=THT]

nets:
  N1: M1.GND, A2.Pin_2, A2.Pin_21
  N2: M1.Tx, A2.Pin_16
  N3: M1.Vcc, A2.Pin_22
  N4: A2.Pin_13, R3.Pin_0
  N5: A2.Pin_14, R4.Pin_0
  N6: A2.Pin_20, R3.Pin_1, R4.Pin_1

custom parts:
  NEO-6M GPS Module: GY-GPS6MV2 NEO-6M GPS Module Module based on U-blox NEO-6M GPS engine, incorporating regulator for 3.3-5V DC input, MS621FE-compatible rechargeable battery for backup and EEPROM for storing configuration settings. Links: NEO-6 series product information page NEO-6 Datasheet
  XIAO ESP32C3-smd: Seeed Studio XIAO ESP32C3 adopts new RISC-V architecture, supporting both Wi-Fi and BLE wireless connectivities.
